# Fritzing sketch BoyScoutRobot (saved by Fritzing 0.9.3b)

parts:
  U1 = NodeMCU V3.0
  U2 = NodeMCU V1.0  # not connected
  HC-SR04_Sensor_1 = HC-SR04 Ultrasonic Distance Sensor
  BATT1 = 4xAA Switchable Battery Pack w/Bare Wire
  M1 = DC Motor
  M2 = DC Motor

nets:
  N1: U1.A-, M2.pin_2
  N2: U1.A+, M2.pin_1
  N3: U1.B-, M1.pin_1
  N4: U1.B+, M1.pin_2
  N5: U1.VIN#49, BATT1.POS
  N6: U1.GND#50, BATT1.NEG
  N7: U1.VIN#51, HC-SR04_Sensor_1.VCC
  N8: U1.GND#52, HC-SR04_Sensor_1.GND
  N9: U1.6, HC-SR04_Sensor_1.ECHO
  N10: U1.5, HC-SR04_Sensor_1.TRIG

notes:
  Power Button
  Jumper

custom parts:
  NodeMCU V3.0: NodeMcu V3 Lua WIFI Development Board
  NodeMCU V1.0: ESP8266 based NodeMCU V1.0
  4xAA Switchable Battery Pack w/Bare Wire: 4xAA Switchable Battery Pack with Bare Wire connection
